// Logisim project Divisao.circ as structural Verilog: 9 circuits, main circuit Main
// Dividendo
module Main (
  input  [15:0] in_1,
  input  [31:0] in_2
);

  wire button_1_out, clock_1_out, divisor_de_32_bits_1_out_5;
  wire [31:0] divisor_de_32_bits_1_out_6, divisor_de_32_bits_1_out_7;

  // Probe on in_1
  // Probe on in_2
  Divisor_de_32_bits divisor_de_32_bits_1 (
    .in_3(in_1), .in_4(in_2), .out_5(divisor_de_32_bits_1_out_5), .out_6(divisor_de_32_bits_1_out_6),
    .out_7(divisor_de_32_bits_1_out_7), .Reset(button_1_out), .Clock(clock_1_out));
  Button button_1 (.out(button_1_out));
  Clock clock_1 (.out(clock_1_out));
  LED led_1 (.in(divisor_de_32_bits_1_out_5));
  // Probe on divisor_de_32_bits_1_out_7
  // Probe on divisor_de_32_bits_1_out_6

  // Notes on the sheet:
  //   Divisor
  //   Dividendo
  //   Divisor em Decimal
  //   Dividendo em Decimal
  //   Quociente em Decimal
  //   Resto em Decimal
endmodule

module Divisor_de_32_bits (
  input  Reset,
  input  Clock,
  input  [15:0] in_3,
  input  [31:0] in_4,
  output out_5,
  output [31:0] out_6,
  output [31:0] out_7
);

  wire and_1_out, and_2_out, and_3_out, and_4_out, and_5_out, resto_1__0, resto_1__0_ou___0;
  wire [1:0] controle_1_out_3;
  wire [31:0] Carrega_Valores_out_5, Carrega_Valores_out_6, Carrega_Valores_out_7, Carrega_Valores_out_8,
       Passo_1_out_7, Passo_1_out_8, Passo_1_out_9, Passo_1_out_10, Passo_2_out_9, Passo_2_out_10,
       Passo_2_out_11, Passo_2_out_12, Passo_3_out_7, Passo_3_out_9, seletor_de_origem_1_out_11,
       seletor_de_origem_1_out_12, seletor_de_origem_1_out_13, seletor_de_origem_1_out_14;

  // Probe on in_3
  // Probe on in_4
  and and_1 (and_1_out, ~Reset, Clock);  // AND_Gate
  Carregar_Valores Carrega_Valores (
    .in_1(in_3), .in_2(in_4), .out_5(Carrega_Valores_out_5), .out_6(Carrega_Valores_out_6),
    .out_7(Carrega_Valores_out_7), .out_8(Carrega_Valores_out_8), .Ativa(and_1_out), .in_4(Reset));
  Controle controle_1 (.out_3(controle_1_out_3), .Proxima_etapa(and_1_out), .out_4(out_5), .Reset(Reset));
  and and_2 (and_2_out, ~controle_1_out_3[1], controle_1_out_3[0]);  // AND_Gate
  and and_3 (and_3_out, ~controle_1_out_3[1], ~controle_1_out_3[0]);  // AND_Gate
  _1_Algoritmo Passo_1 (
    .in_3(seletor_de_origem_1_out_12), .in_4(seletor_de_origem_1_out_11), .in_5(seletor_de_origem_1_out_14),
    .in_6(seletor_de_origem_1_out_13), .out_7(Passo_1_out_7), .out_8(Passo_1_out_8), .out_9(Passo_1_out_9),
    .out_10(Passo_1_out_10), .Enable(and_2_out), .Clear(Reset));
  Seletor_de_Origem seletor_de_origem_1 (
    .Reset(Reset), .in_3(Carrega_Valores_out_6), .in_4(Carrega_Valores_out_5), .in_5(Carrega_Valores_out_7),
    .in_10(Carrega_Valores_out_8), .out_11(seletor_de_origem_1_out_11), .out_12(seletor_de_origem_1_out_12),
    .out_13(seletor_de_origem_1_out_13), .out_14(seletor_de_origem_1_out_14), .in_6(out_7),
    .in_7(Passo_3_out_9), .in_8(out_6), .in_9(Passo_3_out_7), .Inicio(and_3_out));
  and and_4 (and_4_out, controle_1_out_3[1], ~controle_1_out_3[0]);  // AND_Gate
  Resto resto_1 (.in_1(Passo_1_out_7), ._0_ou___0(resto_1__0_ou___0), ._0(resto_1__0));
  _2_Algoritmo Passo_2 (
    .in_4(Passo_1_out_9), .in_5(Passo_1_out_10), .in_6(Passo_1_out_8), .in_7(Passo_1_out_7),
    .out_9(Passo_2_out_9), .out_10(Passo_2_out_10), .out_11(Passo_2_out_11), .out_12(Passo_2_out_12),
    ._0_ou___0(resto_1__0_ou___0), .Enable(and_4_out), .Clear(Reset), ._0(resto_1__0));
  and and_5 (and_5_out, controle_1_out_3[1], controle_1_out_3[0]);
  _3_Algoritmo Passo_3 (
    .in_3(Passo_2_out_9), .in_4(Passo_2_out_12), .in_5(Passo_2_out_11), .in_6(Passo_2_out_10),
    .out_7(Passo_3_out_7), .out_8(out_6), .out_9(Passo_3_out_9), .out_10(out_7), .Enable(and_5_out),
    .Clear(Reset));
  // Probe on out_6
  // Probe on out_7

  // Notes on the sheet:
  //   Divisor
  //   Dividendo
  //   Controle
  //   Fim da Operação (LED)
  //   Seletor de Fonte
  //   Teste do Resto
  //   Resto
  //   Quociente
endmodule

module Carregar_Valores (
  input  [15:0] in_1,
  input  [31:0] in_2,
  input  Ativa,
  input  in_4,
  output [31:0] out_5,
  output [31:0] out_6,
  output [31:0] out_7,
  output [31:0] out_8
);

  wire [31:0] bit_extender_1_out, shifter_1_out;

  Register #(.width(32)) register_1 (.D(in_2), .Q(out_7), .clk(Ativa), .clr(in_4));  // open: en
  Register #(.width(32)) register_2 (.D(in_2), .Q(out_5), .clk(Ativa), .clr(in_4));  // open: en
  assign bit_extender_1_out = {{16{1'b0}}, in_1};  // Bit_Extender bit_extender_1
  Shifter #(.width(32)) shifter_1 (.in(bit_extender_1_out), .\dist (5'b10000), .out(shifter_1_out));
  Register #(.width(32)) register_3 (.D(shifter_1_out), .Q(out_6), .clk(Ativa), .clr(in_4));  // open: en
  Register #(.width(32)) register_4 (.D({32{1'b0}}), .Q(out_8), .clk(Ativa), .clr(in_4));  // open: en
  // Probe on out_6

  // Notes on the sheet:
  //   Divisor
  //   Dividendo
  //   Dividendo
  //   Resto
  //   Carrega valores
  //   Divisor
  //   Quociente
  //   Resto
  //   Divisor
  //   Dividendo
  //   Quociente
endmodule

module Seletor_de_Origem (
  input  Inicio,
  input  Reset,
  input  [31:0] in_3,
  input  [31:0] in_4,
  input  [31:0] in_5,
  input  [31:0] in_6,
  input  [31:0] in_7,
  input  [31:0] in_8,
  input  [31:0] in_9,
  input  [31:0] in_10,
  output [31:0] out_11,
  output [31:0] out_12,
  output [31:0] out_13,
  output [31:0] out_14
);

  wire or_1_out;
  wire [4:0] counter_1_q;

  Counter #(.width(5), .max('h11)) counter_1 (
    .Q(counter_1_q), .clk(Inicio), .clr(Reset));  // open: load, D, count, carry
  Multiplexer #(.width(32), .enable("false")) multiplexer_1 (.in0(in_10), .in1(in_6), .out(out_14), .sel(or_1_out));
  or or_1 (or_1_out, counter_1_q[4], counter_1_q[3], counter_1_q[2], counter_1_q[1], counter_1_q[0]);
  Multiplexer #(.width(32), .enable("false")) multiplexer_2 (.in0(in_5), .in1(in_7), .out(out_13), .sel(or_1_out));
  Multiplexer #(.width(32), .enable("false")) multiplexer_3 (.in0(in_4), .in1(in_8), .out(out_12), .sel(or_1_out));
  Multiplexer #(.width(32), .enable("false")) multiplexer_4 (.in0(in_3), .in1(in_9), .out(out_11), .sel(or_1_out));

  // Notes on the sheet:
  //   Divisor
  //   Resto
  //   Dividendo
  //   Quociente
  //   Quociente
  //   Seletor De Origem
  //   Dividendo
  //   Resto
  //   Divisor
  //   Divisor
  //   Resto
  //   Dividendo
  //   Quociente
endmodule

module _1_Algoritmo (
  input  Enable,
  input  Clear,
  input  [31:0] in_3,
  input  [31:0] in_4,
  input  [31:0] in_5,
  input  [31:0] in_6,
  output [31:0] out_7,
  output [31:0] out_8,
  output [31:0] out_9,
  output [31:0] out_10
);

  wire [31:0] subtractor_1_out;

  Subtractor #(.width(32)) subtractor_1 (.a(in_3), .b(in_4), .out(subtractor_1_out));  // open: bin, bout
  Register #(.width(32)) register_1 (.D(subtractor_1_out), .Q(out_7), .clk(Enable), .clr(Clear));  // open: en
  Register #(.width(32)) register_2 (.D(in_4), .Q(out_8), .clk(Enable), .clr(Clear));  // open: en
  Register #(.width(32)) register_3 (.D(in_5), .Q(out_9), .clk(Enable), .clr(Clear));  // open: en
  Register #(.width(32)) register_4 (.D(in_6), .Q(out_10), .clk(Enable), .clr(Clear));  // open: en
  // Probe on out_7

  // Notes on the sheet:
  //   Resto
  //   Divisor
  //   Quociente
  //   Dividendo
  //   Algoritmo 1
  //   Resto
  //   Divisor
  //   Quociente
  //   Dividendo
endmodule

module Resto (
  input  [31:0] in_1,
  output _0_ou___0,
  output _0
);

  Comparator #(.width(32)) comparator_1 (.a(in_1), .b({32{1'b0}}), .lt(_0));  // open: gt, eq
  not not_1 (_0_ou___0, _0);

  // Notes on the sheet:
  //   Resto
endmodule

module _2_Algoritmo (
  input  Enable,
  input  Clear,
  input  _0_ou___0,
  input  [31:0] in_4,
  input  [31:0] in_5,
  input  [31:0] in_6,
  input  [31:0] in_7,
  input  _0,
  output [31:0] out_9,
  output [31:0] out_10,
  output [31:0] out_11,
  output [31:0] out_12
);

  wire not_1_out;
  wire [31:0] adder_1_out, adder_2_out, controlled_buffer_1_out, controlled_buffer_2_out, shifter_1_out;

  Shifter #(.width(32)) shifter_1 (.in(in_4), .\dist (5'b00001), .out(shifter_1_out));
  Adder #(.width(32)) adder_1 (.a(shifter_1_out), .b(32'h1), .out(adder_1_out));  // open: cin, cout
  Adder #(.width(32)) adder_2 (.a(in_6), .b(in_7), .out(adder_2_out));  // open: cin, cout
  assign controlled_buffer_1_out = not_1_out ? in_7 : 32'bz;  // Controlled_Buffer controlled_buffer_1
  not not_1 (not_1_out, _0);
  assign controlled_buffer_2_out = _0_ou___0 ? adder_1_out : 32'bz;  // Controlled_Buffer controlled_buffer_2
  assign controlled_buffer_2_out = _0 ? shifter_1_out : 32'bz;  // Controlled_Buffer controlled_buffer_3
  assign controlled_buffer_1_out = _0 ? adder_2_out : 32'bz;  // Controlled_Buffer controlled_buffer_4
  Register #(.width(32)) register_1 (.D(in_6), .Q(out_9), .clk(Enable), .clr(Clear));  // open: en
  Register #(.width(32)) register_2 (.D(controlled_buffer_2_out), .Q(out_10), .clk(Enable), .clr(Clear));  // open: en
  Register #(.width(32)) register_3 (.D(in_5), .Q(out_11), .clk(Enable), .clr(Clear));  // open: en
  Register #(.width(32)) register_4 (.D(controlled_buffer_1_out), .Q(out_12), .clk(Enable), .clr(Clear));  // open: en

  // Notes on the sheet:
  //   Quociente
  //   Dividendo
  //   Divisor
  //   Resto
  //   Algoritmo 2
  //   Dividendo
  //   Resto
  //   Divisor
  //   Quociente
endmodule

module _3_Algoritmo (
  input  Enable,
  input  Clear,
  input  [31:0] in_3,
  input  [31:0] in_4,
  input  [31:0] in_5,
  input  [31:0] in_6,
  output [31:0] out_7,
  output [31:0] out_8,
  output [31:0] out_9,
  output [31:0] out_10
);

  wire [31:0] shifter_1_out;

  Shifter #(.width(32), .shift("lr")) shifter_1 (.in(in_3), .\dist (5'b00001), .out(shifter_1_out));
  Register #(.width(32)) register_1 (.D(shifter_1_out), .Q(out_7), .clk(Enable), .clr(Clear));  // open: en
  Register #(.width(32)) register_2 (.D(in_4), .Q(out_8), .clk(Enable), .clr(Clear));  // open: en
  Register #(.width(32)) register_3 (.D(in_5), .Q(out_9), .clk(Enable), .clr(Clear));  // open: en
  Register #(.width(32)) register_4 (.D(in_6), .Q(out_10), .clk(Enable), .clr(Clear));  // open: en

  // Notes on the sheet:
  //   Divisor
  //   Resto
  //   Dividendo
  //   Quociente
  //   Algoritmo 3
  //   Divisor
  //   Resto
  //   Dividendo
  //   Quociente
endmodule

module Controle (
  input  Proxima_etapa,
  input  Reset,
  output [1:0] out_3,
  output out_4
);

  wire and_1_out, counter_1_carry, not_1_out;

  and and_1 (and_1_out, ~Proxima_etapa, not_1_out);  // AND_Gate
  Counter #(.width(2), .max('h3)) counter_1 (
    .Q(out_3), .carry(counter_1_carry), .clk(and_1_out), .clr(Reset));  // open: load, D, count
  not not_1 (not_1_out, out_4);
  LED led_1 (.in(out_3[1]));
  LED led_2 (.in(out_3[0]));
  Counter #(.width(5), .max('h11), .ongoal("stay")) counter_2 (
    .carry(out_4), .clk(counter_1_carry), .clr(Reset));  // open: load, D, count, Q

  // Notes on the sheet:
  //   Seletor de etapas
  //   Seletor de etapas
  //   Fim
  //   Ciclos
endmodule
