// Logisim project MIPS 32bitsv3.circ as structural Verilog: 9 circuits, main circuit Controle
// Fim de Programa
module MIPS_32_bits_Simplificado (
  input  [31:0] VALOR,
  input  [4:0] \Endereço_Registrador ,
  input  Enable,
  input  Ativa_interface,
  input  Escrever_no_Registrador,
  input  [31:0] \Endereço_Memória 
);

  wire alu_32_bits_1_out_7, and_1_out, and_2_out, controle_1_atuapc, controle_1_branch, controle_1_clearalu,
       controle_1_clock, controle_1_escrevemem, controle_1_escrevereg, controle_1_fim_de_programa,
       controle_1_jump, controle_1_lemem, controle_1_memparareg, controle_1_origalu, controle_1_regdst,
       GRAVAR, not_1_out, not_2_out, not_3_out, or_1_out, or_2_out, or_3_out, or_4_out, or_5_out;
  wire [1:0] controle_1_opalu;
  wire [2:0] \controle_alu_1_função ;
  wire [4:0] \memoria_de_instruções_1_dado_1 , \memoria_de_instruções_1_dado_2 ,
       \memoria_de_instruções_1_destino , multiplexer_1_out, multiplexer_2_out, multiplexer_3_out;
  wire [5:0] \extensão_de_sinal_1_instrução__5__0 , \memoria_de_instruções_1_opcode ;
  wire [15:0] \memoria_de_instruções_1_instrução__0_15 ;
  wire [23:0] jump_adress_1_jump_branch, \memoria_de_instruções_1_pc_1 ;
  wire [31:0] alu_32_bits_1_result, banco_de_registradores_1_dados_de_leitura_1,
       banco_de_registradores_1_dados_de_leitura_2, demultiplexer_1_out0, demultiplexer_1_out1,
       \extensão_de_sinal_1_resultado_extens__sinal , memoria_1_output__retorna_ao_b__reg, multiplexer_4_out,
       multiplexer_5_out, multiplexer_6_out, multiplexer_7_out, multiplexer_8_out;

  \Memoria_de_Instruções  \memoria_de_instruções_1  (
    .AtuaPC(controle_1_atuapc), .Destino(\memoria_de_instruções_1_destino ),
    .Dado_1(\memoria_de_instruções_1_dado_1 ), .Dado_2(\memoria_de_instruções_1_dado_2 ),
    .opcode(\memoria_de_instruções_1_opcode ), .\Instrução__0_15 (\memoria_de_instruções_1_instrução__0_15 ),
    .Jump_IF(jump_adress_1_jump_branch), .PC_1(\memoria_de_instruções_1_pc_1 ), .Controle(or_1_out));
  or or_1 (or_1_out, controle_1_jump, controle_1_branch);
  Multiplexer #(.width(5), .enable("false")) multiplexer_1 (
    .in0(\memoria_de_instruções_1_dado_2 ), .in1(\memoria_de_instruções_1_destino ), .out(multiplexer_1_out),
    .sel(controle_1_regdst));
  Jump_Adress jump_adress_1 (
    .Controle_Jump(controle_1_jump), .Controle_Branch(controle_1_branch), .Branch_ALU(alu_32_bits_1_out_7),
    .\Instrução ({\memoria_de_instruções_1_dado_2 [2:0], \memoria_de_instruções_1_dado_1 , \memoria_de_instruções_1_instrução__0_15 }),
    .PC_1(\memoria_de_instruções_1_pc_1 ), .\Instrução_ALU (\extensão_de_sinal_1_resultado_extens__sinal ),
    .Jump_Branch(jump_adress_1_jump_branch));
  Controle controle_1 (
    .opcode(\memoria_de_instruções_1_opcode ), .OpAlu(controle_1_opalu), .OrigALU(controle_1_origalu),
    .EscreveMem(controle_1_escrevemem), .LeMem(controle_1_lemem), .MemParaReg(controle_1_memparareg),
    .RegDst(controle_1_regdst), .EscreveReg(controle_1_escrevereg), .Jump(controle_1_jump),
    .Branch(controle_1_branch), .AtuaPC(controle_1_atuapc), .ClearALU(controle_1_clearalu),
    .Fim_de_Programa(controle_1_fim_de_programa), .Enable(Enable), .Clock(controle_1_clock));
  not not_1 (not_1_out, Ativa_interface);
  Multiplexer #(.width(5), .enable("false")) multiplexer_2 (
    .in0(\Endereço_Registrador ), .in1(\memoria_de_instruções_1_dado_1 ), .out(multiplexer_2_out),
    .sel(not_1_out));
  Multiplexer #(.width(5), .enable("false")) multiplexer_3 (
    .in0(\Endereço_Registrador ), .in1(multiplexer_1_out), .out(multiplexer_3_out), .sel(not_1_out));
  Multiplexer #(.width(32), .enable("false")) multiplexer_4 (
    .in0(VALOR), .in1(multiplexer_6_out), .out(multiplexer_4_out), .sel(not_1_out));
  and and_1 (and_1_out, Escrever_no_Registrador, Ativa_interface);
  or or_2 (or_2_out, and_1_out, controle_1_escrevereg);
  \Extensão_de_sinal  \extensão_de_sinal_1  (
    .\instrução_15_0 (\memoria_de_instruções_1_instrução__0_15 ),
    .Resultado_extens__sinal(\extensão_de_sinal_1_resultado_extens__sinal ),
    .\Instrução__5__0 (\extensão_de_sinal_1_instrução__5__0 ));
  and and_2 (and_2_out, Ativa_interface, GRAVAR);
  or or_3 (or_3_out, controle_1_clock, and_2_out);
  Banco_de_Registradores banco_de_registradores_1 (
    .Clock(or_3_out), .Registrador_de_leitura_1(multiplexer_2_out),
    .Registrador_de_leitura_2(\memoria_de_instruções_1_dado_2 ),
    .Registrador_para_escrita(multiplexer_3_out),
    .Dados_de_leitura_1(banco_de_registradores_1_dados_de_leitura_1), .Escreve_Reg(or_2_out),
    .Dados_de_leitura_2(banco_de_registradores_1_dados_de_leitura_2), .Dados_para_escrita(multiplexer_4_out),
    .Enable(Enable));
  Demultiplexer #(.width(32), .enable("false")) demultiplexer_1 (
    .out0(demultiplexer_1_out0), .out1(demultiplexer_1_out1),
    .in(banco_de_registradores_1_dados_de_leitura_1), .sel(Ativa_interface));
  Controle_ALU controle_alu_1 (
    .OpAlu1(controle_1_opalu), .\Instruçao_5__0 (\extensão_de_sinal_1_instrução__5__0 ),
    .\função (\controle_alu_1_função ));
  ALU_32_bits alu_32_bits_1 (
    .OrigALU(controle_1_origalu), .out_7(alu_32_bits_1_out_7), .Input_ALU_1(demultiplexer_1_out0),
    .Input_ALU_2(banco_de_registradores_1_dados_de_leitura_2), .RESULT(alu_32_bits_1_result),
    .\EXTENSÃO (\extensão_de_sinal_1_resultado_extens__sinal ), .Clear(controle_1_clearalu),
    .Controle_ALU(\controle_alu_1_função ));
  LED led_1 (.in(controle_1_fim_de_programa));
  not not_2 (not_2_out, Ativa_interface);
  Multiplexer #(.width(32), .enable("false")) multiplexer_5 (
    .in0(\Endereço_Memória ), .in1(alu_32_bits_1_result), .out(multiplexer_5_out), .sel(not_2_out));
  or or_4 (or_4_out, controle_1_lemem, Ativa_interface);
  or or_5 (or_5_out, controle_1_clock, Ativa_interface);
  Memoria memoria_1 (
    .Resultado_da_ALU(multiplexer_5_out), .Input_de_dados(banco_de_registradores_1_dados_de_leitura_2),
    .Output__retorna_ao_b__reg(memoria_1_output__retorna_ao_b__reg), .LeMem(or_4_out), .Clock(or_5_out),
    .EscreveMem(controle_1_escrevemem), .Enable(Enable));
  not not_3 (not_3_out, controle_1_memparareg);
  Multiplexer #(.width(32), .enable("false")) multiplexer_6 (
    .in0(memoria_1_output__retorna_ao_b__reg), .in1(alu_32_bits_1_result), .out(multiplexer_6_out),
    .sel(not_3_out));
  Multiplexer #(.width(32), .enable("false")) multiplexer_7 (
    .in1(memoria_1_output__retorna_ao_b__reg), .out(multiplexer_7_out), .sel(Ativa_interface));  // open: in0
  Multiplexer #(.width(32), .enable("false")) multiplexer_8 (
    .in1(demultiplexer_1_out1), .out(multiplexer_8_out), .sel(Ativa_interface));  // open: in0
  Hex_Digit_Display hex_digit_display_1 (.value(multiplexer_7_out[27:24]));  // open: dp
  Hex_Digit_Display hex_digit_display_2 (.value(multiplexer_7_out[31:28]));  // open: dp
  Hex_Digit_Display hex_digit_display_3 (.value(multiplexer_8_out[27:24]));  // open: dp
  Hex_Digit_Display hex_digit_display_4 (.value(multiplexer_8_out[31:28]));  // open: dp
  Button Gravar_no_Registrador (.out(GRAVAR));
  Hex_Digit_Display hex_digit_display_5 (.value(multiplexer_7_out[23:20]));  // open: dp
  Hex_Digit_Display hex_digit_display_6 (.value(multiplexer_8_out[23:20]));  // open: dp
  // Probe on VALOR
  // Probe on \Endereço_Registrador 
  Hex_Digit_Display hex_digit_display_7 (.value(multiplexer_7_out[19:16]));  // open: dp
  Hex_Digit_Display hex_digit_display_8 (.value(multiplexer_8_out[19:16]));  // open: dp
  Hex_Digit_Display hex_digit_display_9 (.value(multiplexer_7_out[15:12]));  // open: dp
  Hex_Digit_Display hex_digit_display_10 (.value(multiplexer_7_out[11:8]));  // open: dp
  Hex_Digit_Display hex_digit_display_11 (.value(multiplexer_8_out[15:12]));  // open: dp
  Hex_Digit_Display hex_digit_display_12 (.value(multiplexer_8_out[11:8]));  // open: dp
  Hex_Digit_Display hex_digit_display_13 (.value(multiplexer_7_out[7:4]));  // open: dp
  Hex_Digit_Display hex_digit_display_14 (.value(multiplexer_8_out[7:4]));  // open: dp
  Hex_Digit_Display hex_digit_display_15 (.value(multiplexer_7_out[3:0]));  // open: dp
  Hex_Digit_Display hex_digit_display_16 (.value(multiplexer_8_out[3:0]));  // open: dp

  // Other names for the same wires on the sheet: EndMem[31:0] = \Endereço_Memória ;
  //   EndReg[4:0] = \Endereço_Registrador ; EscreverReg = Escrever_no_Registrador

  // Notes on the sheet:
  //   Enable
  //   Reg. Leit. 1
  //   Reg. Leit. 2
  //   Registrador para Escrita
  //   Dados para escrita
  //   EscreveReg
  //   Clock
  //   Dados de leitura 1
  //   Banco de
  //   Registradores
  //   Dados de leitura 2
  //   FIM DE PROGRAMA
  //   LeMem
  //   Endereco
  //   Dados para escrita
  //   Clock
  //   Memória de Dados
  //   Enable
  //   EscreveMem
endmodule

module Controle (
  input  [5:0] opcode,
  input  Enable,
  output [1:0] OpAlu,
  output OrigALU,
  output EscreveMem,
  output LeMem,
  output MemParaReg,
  output RegDst,
  output EscreveReg,
  output Jump,
  output Branch,
  output AtuaPC,
  output ClearALU,
  output Fim_de_Programa,
  output Clock
);

  wire and_2_out, and_3_out, clock_1_out, comparator_1_eq, not_1_out, not_2_out, not_3_out, not_4_out,
       not_5_out, not_6_out, not_7_out, not_8_out, not_9_out, not_10_out, not_11_out, not_12_out, not_13_out,
       not_14_out, not_15_out, not_16_out, not_17_out, not_18_out, not_19_out, not_20_out, not_21_out,
       not_22_out, not_23_out, not_24_out, or_1_out, or_2_out, or_3_out, or_4_out, or_5_out, or_6_out,
       or_7_out;
  wire [6:0] counter_1_q;

  and and_1 (Fim_de_Programa, opcode[5], opcode[4], opcode[3], opcode[2], opcode[1], opcode[0]);
  not not_1 (not_1_out, Fim_de_Programa);
  not not_2 (not_2_out, opcode[0]);
  not not_3 (not_3_out, opcode[1]);
  not not_4 (not_4_out, opcode[2]);
  not not_5 (not_5_out, opcode[3]);
  not not_6 (not_6_out, opcode[4]);
  not not_7 (not_7_out, opcode[5]);
  not not_8 (not_8_out, opcode[2]);
  not not_9 (not_9_out, opcode[3]);
  not not_10 (not_10_out, opcode[4]);
  not not_11 (not_11_out, opcode[2]);
  not not_12 (not_12_out, opcode[4]);
  not not_13 (not_13_out, opcode[0]);
  not not_14 (not_14_out, opcode[2]);
  not not_15 (not_15_out, opcode[3]);
  not not_16 (not_16_out, opcode[4]);
  not not_17 (not_17_out, opcode[5]);
  not not_18 (not_18_out, opcode[0]);
  not not_19 (not_19_out, opcode[1]);
  not not_20 (not_20_out, opcode[3]);
  not not_21 (not_21_out, opcode[4]);
  not not_22 (not_22_out, opcode[5]);
  Clock clock_1 (.out(clock_1_out));
  and and_2 (and_2_out, not_2_out, not_3_out, not_4_out, not_5_out, not_6_out, not_7_out);
  and and_3 (and_3_out, opcode[0], opcode[1], not_8_out, not_9_out, not_10_out, opcode[5]);
  and and_4 (and_3_out, opcode[0], opcode[1], not_11_out, opcode[3], not_12_out, opcode[5]);
  and and_5 (Jump, not_13_out, opcode[1], not_14_out, not_15_out, not_16_out, not_17_out);
  and and_6 (Branch, not_18_out, not_19_out, opcode[2], not_20_out, not_21_out, not_22_out);
  and and_7 (Clock, not_1_out, Enable, clock_1_out);
  Counter #(.width(7), .max('h46)) counter_1 (
    .Q(counter_1_q), .clk(Clock), .clr(not_23_out));  // open: load, D, count, carry
  not not_23 (not_23_out, Enable);
  or or_1 (or_1_out, and_2_out, Branch);
  or or_2 (or_2_out, and_3_out, and_3_out);
  buf or_3 (or_3_out, and_3_out);  // OR_Gate
  buf or_4 (or_4_out, and_3_out);  // OR_Gate
  buf or_5 (or_5_out, and_3_out);  // OR_Gate
  buf or_6 (or_6_out, and_2_out);  // OR_Gate
  or or_7 (or_7_out, and_2_out, and_3_out);
  Comparator #(.width(7)) comparator_1 (.a(counter_1_q), .b(7'b1000110), .eq(comparator_1_eq));  // open: gt, lt
  Comparator #(.width(7)) comparator_2 (.a(counter_1_q), .b({7{1'b0}}), .eq(AtuaPC));  // open: gt, lt
  Comparator #(.width(7)) comparator_3 (.a(counter_1_q), .b(7'b0000001), .eq(ClearALU));  // open: gt, lt
  and and_8 (OpAlu[1], or_1_out, not_24_out);
  and and_9 (OrigALU, or_2_out, not_24_out);
  and and_10 (EscreveMem, or_3_out, comparator_1_eq);
  and and_11 (LeMem, or_4_out, comparator_1_eq);
  and and_12 (MemParaReg, or_5_out, not_24_out);
  not not_24 (not_24_out, AtuaPC);
  and and_13 (RegDst, or_6_out, comparator_1_eq);
  and and_14 (EscreveReg, or_7_out, comparator_1_eq);

  assign OpAlu[0] = 1'b0;

  // Notes on the sheet:
  //   Clock: pull=up
  //   Formato R
  //   load word
  //   store word
  //   jump
  //   beq
  //   Não zero
  //   zero
  //   não zero
  //   70
  //   69
  //   70
  //   70
endmodule

module \Memoria_de_Instruções  (
  input  Controle,
  input  [23:0] Jump_IF,
  input  AtuaPC,
  output [23:0] PC_1,
  output [4:0] Destino,
  output [4:0] Dado_1,
  output [4:0] Dado_2,
  output [5:0] opcode,
  output [15:0] \Instrução__0_15 
);

  wire \Limpar_instruções_out , not_1_out, zerar_contagem_out;
  wire [4:0] ram_1_data;
  wire [23:0] counter_1_q;

  Button zerar_contagem (.out(zerar_contagem_out));
  Button \Limpar_instruções  (.out(\Limpar_instruções_out ));
  Counter #(.width(24), .max('hffffff)) counter_1 (
    .load(Controle), .D(Jump_IF), .count(not_1_out), .Q(counter_1_q), .clk(AtuaPC), .clr(zerar_contagem_out));  // open: carry
  not not_1 (not_1_out, Controle);
  RAM #(.addrWidth(24), .dataWidth(32)) ram_1 (
    .addr(counter_1_q), .data({opcode, ram_1_data, Dado_2, \Instrução__0_15 }), .clk(AtuaPC), .ld(1'b1),
    .clr(\Limpar_instruções_out ));  // open: sel
  Adder #(.width(24)) adder_1 (.a(counter_1_q), .b(24'h1), .out(PC_1));  // open: cin, cout
  Multiplexer #(.width(5), .enable("false")) multiplexer_1 (
    .in0(\Instrução__0_15 [15:11]), .in1(\Instrução__0_15 [10:6]), .out(Destino), .sel(opcode[4]));
  Multiplexer #(.width(5), .enable("false")) multiplexer_2 (
    .in0(ram_1_data), .in1(\Instrução__0_15 [15:11]), .out(Dado_1), .sel(opcode[4]));

  // Notes on the sheet:
  //   [11:15]
  //   [6:10]
  //   [21:25]
  //   [20:16]
  //   [26:31]
  //   [0:15]
  //   Operação floating
endmodule

module Banco_de_Registradores (
  input  Escreve_Reg,
  input  Clock,
  input  [4:0] Registrador_de_leitura_1,
  input  [4:0] Registrador_de_leitura_2,
  input  [31:0] Dados_para_escrita,
  input  [4:0] Registrador_para_escrita,
  input  Enable,
  output [31:0] Dados_de_leitura_1,
  output [31:0] Dados_de_leitura_2
);

  wire _0_out, _1_out, _2_out, _3_out, _4_out, _5_out, _6_out, _7_out, _8_out, _9_out, _10_out, _11_out,
       _12_out, _13_out, _14_out, _15_out, _16_out, _17_out, _18_out, _19_out, _20_out, _21_out, _22_out,
       _23_out, _24_out, _25_out, _26_out, _27_out, _28_out, _29_out, _30_out, _31_out, decoder_1_out0,
       decoder_1_out1, decoder_2_out0, decoder_2_out1, decoder_2_out2, decoder_2_out3, decoder_2_out4,
       decoder_2_out5, decoder_2_out6, decoder_2_out7, decoder_2_out8, decoder_2_out9, decoder_2_out10,
       decoder_2_out11, decoder_2_out12, decoder_2_out13, decoder_2_out14, decoder_2_out15, decoder_2_out16,
       decoder_2_out17, decoder_2_out18, decoder_2_out19, decoder_2_out20, decoder_2_out21, decoder_2_out22,
       decoder_2_out23, decoder_2_out24, decoder_2_out25, decoder_2_out26, decoder_2_out27, decoder_2_out28,
       decoder_2_out29, decoder_2_out30, decoder_2_out31, not_1_out;
  wire [31:0] register_1_q, register_2_q, register_3_q, register_4_q, register_5_q, register_6_q,
       register_7_q, register_8_q, register_9_q, register_10_q, register_11_q, register_12_q, register_13_q,
       register_14_q, register_15_q, register_16_q, register_17_q, register_18_q, register_19_q,
       register_20_q, register_21_q, register_22_q, register_23_q, register_24_q, register_25_q,
       register_26_q, register_27_q, register_28_q, register_29_q, register_30_q, register_31_q,
       register_32_q;

  not not_1 (not_1_out, Enable);
  Decoder #(.enable("false")) decoder_1 (.out0(decoder_1_out0), .out1(decoder_1_out1), .sel(Escreve_Reg));
  Decoder #(.select(5), .enable("false")) decoder_2 (
    .out0(decoder_2_out0), .out1(decoder_2_out1), .out2(decoder_2_out2), .out3(decoder_2_out3),
    .out4(decoder_2_out4), .out5(decoder_2_out5), .out6(decoder_2_out6), .out7(decoder_2_out7),
    .out8(decoder_2_out8), .out9(decoder_2_out9), .out10(decoder_2_out10), .out11(decoder_2_out11),
    .out12(decoder_2_out12), .out13(decoder_2_out13), .out14(decoder_2_out14), .out15(decoder_2_out15),
    .out16(decoder_2_out16), .out17(decoder_2_out17), .out18(decoder_2_out18), .out19(decoder_2_out19),
    .out20(decoder_2_out20), .out21(decoder_2_out21), .out22(decoder_2_out22), .out23(decoder_2_out23),
    .out24(decoder_2_out24), .out25(decoder_2_out25), .out26(decoder_2_out26), .out27(decoder_2_out27),
    .out28(decoder_2_out28), .out29(decoder_2_out29), .out30(decoder_2_out30), .out31(decoder_2_out31),
    .sel(Registrador_para_escrita));
  Register #(.width(32), .trigger("falling")) register_1 (
    .D(Dados_para_escrita), .en(_0_out), .Q(register_1_q), .clk(Clock), .clr(not_1_out));
  and _0 (_0_out, decoder_2_out0, decoder_1_out1);
  Register #(.width(32), .trigger("falling")) register_2 (
    .D(Dados_para_escrita), .en(_4_out), .Q(register_2_q), .clk(Clock), .clr(not_1_out));
  and _4 (_4_out, decoder_2_out4, decoder_1_out1);
  Register #(.width(32), .trigger("falling")) register_3 (
    .D(Dados_para_escrita), .en(_8_out), .Q(register_3_q), .clk(Clock), .clr(not_1_out));
  and _8 (_8_out, decoder_2_out8, decoder_1_out1);
  Register #(.width(32), .trigger("falling")) register_4 (
    .D(Dados_para_escrita), .en(_12_out), .Q(register_4_q), .clk(Clock), .clr(not_1_out));
  and _12 (_12_out, decoder_2_out12, decoder_1_out1);
  Register #(.width(32), .trigger("falling")) register_5 (
    .D(Dados_para_escrita), .en(_16_out), .Q(register_5_q), .clk(Clock), .clr(not_1_out));
  and _16 (_16_out, decoder_2_out16, decoder_1_out1);
  Register #(.width(32), .trigger("falling")) register_6 (
    .D(Dados_para_escrita), .en(_20_out), .Q(register_6_q), .clk(Clock), .clr(not_1_out));
  and _20 (_20_out, decoder_2_out20, decoder_1_out1);
  and _24 (_24_out, decoder_2_out24, decoder_1_out1);
  and _28 (_28_out, decoder_2_out28, decoder_1_out1);
  Register #(.width(32), .trigger("falling")) register_7 (
    .D(Dados_para_escrita), .en(_24_out), .Q(register_7_q), .clk(Clock), .clr(not_1_out));
  Register #(.width(32), .trigger("falling")) register_8 (
    .D(Dados_para_escrita), .en(_28_out), .Q(register_8_q), .clk(Clock), .clr(not_1_out));
  Register #(.width(32), .trigger("falling")) register_9 (
    .D(Dados_para_escrita), .en(_1_out), .Q(register_9_q), .clk(Clock), .clr(not_1_out));
  and _1 (_1_out, decoder_2_out1, decoder_1_out1);
  Register #(.width(32), .trigger("falling")) register_10 (
    .D(Dados_para_escrita), .en(_5_out), .Q(register_10_q), .clk(Clock), .clr(not_1_out));
  and _5 (_5_out, decoder_2_out5, decoder_1_out1);
  Register #(.width(32), .trigger("falling")) register_11 (
    .D(Dados_para_escrita), .en(_9_out), .Q(register_11_q), .clk(Clock), .clr(not_1_out));
  and _9 (_9_out, decoder_2_out9, decoder_1_out1);
  Register #(.width(32), .trigger("falling")) register_12 (
    .D(Dados_para_escrita), .en(_13_out), .Q(register_12_q), .clk(Clock), .clr(not_1_out));
  and _13 (_13_out, decoder_2_out13, decoder_1_out1);
  Register #(.width(32), .trigger("falling")) register_13 (
    .D(Dados_para_escrita), .en(_17_out), .Q(register_13_q), .clk(Clock), .clr(not_1_out));
  and _17 (_17_out, decoder_2_out17, decoder_1_out1);
  Register #(.width(32), .trigger("falling")) register_14 (
    .D(Dados_para_escrita), .en(_21_out), .Q(register_14_q), .clk(Clock), .clr(not_1_out));
  and _21 (_21_out, decoder_2_out21, decoder_1_out1);
  and _25 (_25_out, decoder_2_out25, decoder_1_out1);
  and _29 (_29_out, decoder_2_out29, decoder_1_out1);
  Register #(.width(32), .trigger("falling")) register_15 (
    .D(Dados_para_escrita), .en(_25_out), .Q(register_15_q), .clk(Clock), .clr(not_1_out));
  Register #(.width(32), .trigger("falling")) register_16 (
    .D(Dados_para_escrita), .en(_29_out), .Q(register_16_q), .clk(Clock), .clr(not_1_out));
  Register #(.width(32), .trigger("falling")) register_17 (
    .D(Dados_para_escrita), .en(_2_out), .Q(register_17_q), .clk(Clock), .clr(not_1_out));
  and _2 (_2_out, decoder_2_out2, decoder_1_out1);
  Register #(.width(32), .trigger("falling")) register_18 (
    .D(Dados_para_escrita), .en(_6_out), .Q(register_18_q), .clk(Clock), .clr(not_1_out));
  and _6 (_6_out, decoder_2_out6, decoder_1_out1);
  Register #(.width(32), .trigger("falling")) register_19 (
    .D(Dados_para_escrita), .en(_10_out), .Q(register_19_q), .clk(Clock), .clr(not_1_out));
  and _10 (_10_out, decoder_2_out10, decoder_1_out1);
  Register #(.width(32), .trigger("falling")) register_20 (
    .D(Dados_para_escrita), .en(_14_out), .Q(register_20_q), .clk(Clock), .clr(not_1_out));
  and _14 (_14_out, decoder_2_out14, decoder_1_out1);
  Register #(.width(32), .trigger("falling")) register_21 (
    .D(Dados_para_escrita), .en(_18_out), .Q(register_21_q), .clk(Clock), .clr(not_1_out));
  and _18 (_18_out, decoder_2_out18, decoder_1_out1);
  Register #(.width(32), .trigger("falling")) register_22 (
    .D(Dados_para_escrita), .en(_22_out), .Q(register_22_q), .clk(Clock), .clr(not_1_out));
  and _22 (_22_out, decoder_2_out22, decoder_1_out1);
  Register #(.width(32), .trigger("falling")) register_23 (
    .D(Dados_para_escrita), .en(_26_out), .Q(register_23_q), .clk(Clock), .clr(not_1_out));
  and _26 (_26_out, decoder_2_out26, decoder_1_out1);
  Register #(.width(32), .trigger("falling")) register_24 (
    .D(Dados_para_escrita), .en(_30_out), .Q(register_24_q), .clk(Clock), .clr(not_1_out));
  and _30 (_30_out, decoder_2_out30, decoder_1_out1);
  and _7 (_7_out, decoder_2_out7, decoder_1_out1);
  and _11 (_11_out, decoder_2_out11, decoder_1_out1);
  and _15 (_15_out, decoder_2_out15, decoder_1_out1);
  and _19 (_19_out, decoder_2_out19, decoder_1_out1);
  and _23 (_23_out, decoder_2_out23, decoder_1_out1);
  and _31 (_31_out, decoder_2_out31, decoder_1_out1);
  Register #(.width(32), .trigger("falling")) register_25 (
    .D(Dados_para_escrita), .en(_3_out), .Q(register_25_q), .clk(Clock), .clr(not_1_out));
  and _3 (_3_out, decoder_2_out3, decoder_1_out1);
  Register #(.width(32), .trigger("falling")) register_26 (
    .D(Dados_para_escrita), .en(_7_out), .Q(register_26_q), .clk(Clock), .clr(not_1_out));
  Register #(.width(32), .trigger("falling")) register_27 (
    .D(Dados_para_escrita), .en(_11_out), .Q(register_27_q), .clk(Clock), .clr(not_1_out));
  Register #(.width(32), .trigger("falling")) register_28 (
    .D(Dados_para_escrita), .en(_15_out), .Q(register_28_q), .clk(Clock), .clr(not_1_out));
  Register #(.width(32), .trigger("falling")) register_29 (
    .D(Dados_para_escrita), .en(_19_out), .Q(register_29_q), .clk(Clock), .clr(not_1_out));
  Register #(.width(32), .trigger("falling")) register_30 (
    .D(Dados_para_escrita), .en(_23_out), .Q(register_30_q), .clk(Clock), .clr(not_1_out));
  Register #(.width(32), .trigger("falling")) register_31 (
    .D(Dados_para_escrita), .en(_27_out), .Q(register_31_q), .clk(Clock), .clr(not_1_out));
  and _27 (_27_out, decoder_2_out27, decoder_1_out1);
  Register #(.width(32), .trigger("falling")) register_32 (
    .D(Dados_para_escrita), .en(_31_out), .Q(register_32_q), .clk(Clock), .clr(not_1_out));
  Multiplexer #(.select(5), .width(32)) multiplexer_1 (
    .in0(register_1_q), .in1(register_9_q), .in2(register_17_q), .in3(register_25_q), .in4(register_2_q),
    .in5(register_10_q), .in6(register_18_q), .in7(register_26_q), .in8(register_3_q), .in9(register_11_q),
    .in10(register_19_q), .in11(register_27_q), .in12(register_4_q), .in13(register_12_q),
    .in14(register_20_q), .in15(register_28_q), .in16(register_5_q), .in17(register_13_q),
    .in18(register_21_q), .in19(register_29_q), .in20(register_6_q), .in21(register_14_q),
    .in22(register_22_q), .in23(register_30_q), .in24(register_7_q), .in25(register_15_q),
    .in26(register_23_q), .in27(register_31_q), .in28(register_8_q), .in29(register_16_q),
    .in30(register_24_q), .in31(register_32_q), .out(Dados_de_leitura_1), .sel(Registrador_de_leitura_1),
    .en(decoder_1_out0));
  Multiplexer #(.select(5), .width(32)) multiplexer_2 (
    .in0(register_1_q), .in1(register_9_q), .in2(register_17_q), .in3(register_25_q), .in4(register_2_q),
    .in5(register_10_q), .in6(register_18_q), .in7(register_26_q), .in8(register_3_q), .in9(register_11_q),
    .in10(register_19_q), .in11(register_27_q), .in12(register_4_q), .in13(register_12_q),
    .in14(register_20_q), .in15(register_28_q), .in16(register_5_q), .in17(register_13_q),
    .in18(register_21_q), .in19(register_29_q), .in20(register_6_q), .in21(register_14_q),
    .in22(register_22_q), .in23(register_30_q), .in24(register_7_q), .in25(register_15_q),
    .in26(register_23_q), .in27(register_31_q), .in28(register_8_q), .in29(register_16_q),
    .in30(register_24_q), .in31(register_32_q), .out(Dados_de_leitura_2), .sel(Registrador_de_leitura_2),
    .en(decoder_1_out0));
endmodule

module ALU_32_bits (
  input  OrigALU,
  input  [31:0] Input_ALU_1,
  input  [31:0] Input_ALU_2,
  input  [31:0] \EXTENSÃO ,
  input  Clear,
  input  [2:0] Controle_ALU,
  output out_7,
  output [31:0] RESULT
);

  wire [31:0] adder_1_out, And_out, multiplexer_1_out, multiplexer_2_out, multiplier_1_out, Or_out,
       subtractor_1_out;

  Multiplexer #(.width(32), .enable("false")) multiplexer_1 (
    .in0(Input_ALU_2), .in1(\EXTENSÃO ), .out(multiplexer_1_out), .sel(OrigALU));
  assign And_out = Input_ALU_1 & multiplexer_1_out;  // AND_Gate And, 32 bits wide
  assign Or_out = Input_ALU_1 | multiplexer_1_out;  // OR_Gate Or, 32 bits wide
  Adder #(.width(32)) adder_1 (.a(Input_ALU_1), .b(multiplexer_1_out), .out(adder_1_out));  // open: cin, cout
  Subtractor #(.width(32)) subtractor_1 (
    .a(Input_ALU_1), .b(multiplexer_1_out), .out(subtractor_1_out));  // open: bin, bout
  Multiplier #(.width(32)) multiplier_1 (
    .a(Input_ALU_1), .b(multiplexer_1_out), .out(multiplier_1_out));  // open: cin, cout
  // Probe on multiplexer_2_out
  Multiplexer #(.select(3), .width(32), .enable("false")) multiplexer_2 (
    .in0(And_out), .in1(Or_out), .in2(adder_1_out), .in4(multiplier_1_out), .in6(subtractor_1_out),
    .out(multiplexer_2_out), .sel(Controle_ALU));  // open: in3, in5, in7
  Comparator #(.width(32)) comparator_1 (.a({32{1'b0}}), .b(RESULT), .eq(out_7));  // open: gt, lt
  RAM #(.addrWidth(2), .dataWidth(32), .bus("separate")) ram_1 (
    .addr(2'b00), .din(multiplexer_2_out), .data(RESULT), .clr(Clear));  // open: str, sel, clk, ld

  // Notes on the sheet:
  //   0 - Op Aritmetica -> inputAlu1 e inputAlu2
  //   1- Op Logica -> inputAlu1 e extensao
  //   Verifica se o resultado eh menor ou igual a zero
endmodule

module Controle_ALU (
  input  [1:0] OpAlu1,
  input  [5:0] \Instruçao_5__0 ,
  output [2:0] \função 
);

  wire and_1_out, and_2_out, and_3_out, and_4_out, and_6_out, and_7_out, and_8_out, not_1_out, not_2_out,
       not_3_out, not_4_out, not_5_out, not_6_out, not_7_out, not_8_out, or_1_out, or_2_out;

  not not_1 (not_1_out, OpAlu1[1]);
  not not_2 (not_2_out, \Instruçao_5__0 [3]);
  not not_3 (not_3_out, \Instruçao_5__0 [0]);
  not not_4 (not_4_out, \Instruçao_5__0 [1]);
  not not_5 (not_5_out, \Instruçao_5__0 [2]);
  not not_6 (not_6_out, \Instruçao_5__0 [4]);
  and and_1 (and_1_out, OpAlu1[0], not_1_out);
  and and_2 (and_2_out, OpAlu1[1], \Instruçao_5__0 [0]);
  and and_3 (and_3_out, OpAlu1[1], \Instruçao_5__0 [3]);
  and and_4 (and_4_out, OpAlu1[1], \Instruçao_5__0 [1], not_2_out);
  // AND_Gate and_5 has open pins: in0=OpAlu1[1], in1=\Instruçao_5__0 [2], in2=not_3_out, out=open
  and and_6 (and_6_out, OpAlu1[1], not_4_out, not_5_out, not_6_out);
  and and_7 (and_7_out, OpAlu1[1], \Instruçao_5__0 [4]);
  not not_7 (not_7_out, and_1_out);
  and and_8 (and_8_out, not_8_out, not_7_out);
  not not_8 (not_8_out, \Instruçao_5__0 [4]);
  or or_1 (or_1_out, and_1_out, and_4_out);
  or or_2 (or_2_out, and_8_out, and_6_out);
  or or_3 (\função [2], and_7_out, or_1_out, and_3_out);
  or or_4 (\função [1], or_2_out, or_1_out, and_3_out);
  or or_5 (\função [0], and_3_out, and_2_out);

  // Notes on the sheet:
  //   Aritmética
  //   Lógica
  //   Or
  //   slt
  //   sub
  //   and
  //   add
  //   mult
  //   sub (op logica)
  //   add (op logica)
endmodule

module Memoria (
  input  LeMem,
  input  Clock,
  input  EscreveMem,
  input  [31:0] Resultado_da_ALU,
  input  [31:0] Input_de_dados,
  input  Enable,
  output [31:0] Output__retorna_ao_b__reg
);

  wire multiplexer_1_out, not_1_out, not_2_out, or_1_out;

  // Probe on Input_de_dados
  not not_1 (not_1_out, Clock);
  Multiplexer multiplexer_1 (.in0(Clock), .in1(not_1_out), .out(multiplexer_1_out), .sel(EscreveMem));  // open: en
  or or_1 (or_1_out, EscreveMem, LeMem);
  not not_2 (not_2_out, Enable);
  RAM #(.addrWidth(24), .dataWidth(32), .bus("separate")) ram_1 (
    .addr(Resultado_da_ALU[23:0]), .din(Input_de_dados), .data(Output__retorna_ao_b__reg), .str(EscreveMem),
    .sel(or_1_out), .clk(multiplexer_1_out), .ld(LeMem), .clr(not_2_out));
  // also tied to GND on the sheet: {Resultado_da_ALU[24], Resultado_da_ALU[25], Resultado_da_ALU[26], Resultado_da_ALU[27], Resultado_da_ALU[28], Resultado_da_ALU[29], Resultado_da_ALU[30], Resultado_da_ALU[31]}
endmodule

module \Extensão_de_sinal  (
  input  [15:0] \instrução_15_0 ,
  output [31:0] Resultado_extens__sinal,
  output [5:0] \Instrução__5__0 
);

  assign Resultado_extens__sinal = {{16{1'b0}}, \instrução_15_0 };  // Bit_Extender bit_extender_1
  Bit_Extender #(.in_width(16), .out_width(6)) bit_extender_2 (.in(\instrução_15_0 ), .out(\Instrução__5__0 ));
endmodule

module Jump_Adress (
  input  [23:0] \Instrução ,
  input  [23:0] PC_1,
  input  Branch_ALU,
  input  Controle_Branch,
  input  Controle_Jump,
  input  [31:0] \Instrução_ALU ,
  output [23:0] Jump_Branch
);

  wire and_1_out, not_1_out;
  wire [23:0] adder_1_out, bit_extender_1_out, multiplexer_1_out;

  Bit_Extender #(.in_width(32), .out_width(24)) bit_extender_1 (.in(\Instrução_ALU ), .out(bit_extender_1_out));
  Adder #(.width(24)) adder_1 (.a(PC_1), .b(bit_extender_1_out), .out(adder_1_out));  // open: cin, cout
  Multiplexer #(.width(24)) multiplexer_1 (
    .in0(PC_1), .in1(adder_1_out), .out(multiplexer_1_out), .sel(and_1_out), .en(Controle_Branch));
  and and_1 (and_1_out, Branch_ALU, Controle_Branch);
  not not_1 (not_1_out, Controle_Jump);
  Multiplexer #(.width(24), .enable("false")) multiplexer_2 (
    .in0(\Instrução ), .in1(multiplexer_1_out), .out(Jump_Branch), .sel(not_1_out));
endmodule
