// Logisim project SomaSub (float).circ as structural Verilog: 5 circuits, main circuit main
module main (
  input  [31:0] entrada1,
  input  [31:0] entrada2,
  input  \bit_de_operação 
);

  wire \soma_subtração_1_overflow ;
  wire [31:0] \soma_subtração_1_resultado_final ;

  \Soma_Subtração  \soma_subtração_1  (
    .\bit_de_operação (\bit_de_operação ), .entrada1(entrada1), .entrada2(entrada2),
    .RESULTADO_FINAL(\soma_subtração_1_resultado_final ), .OVERFLOW(\soma_subtração_1_overflow ));
  // Probe on \soma_subtração_1_resultado_final 
  // Probe on \soma_subtração_1_overflow 
endmodule

module Verifica_Nulo (
  input  [31:0] entrada2,
  input  [31:0] entrada1,
  output out_3,
  output [31:0] out_4
);

  wire and_1_out, comparator_1_eq, comparator_1_lt, comparator_2_eq, comparator_3_eq, comparator_4_eq,
       comparator_5_eq, comparator_6_eq, En, EXPOENTE_MAIOR_NUMERO, not_1_out;
  wire [1:0] or_1_out;

  Comparator #(.width(31), .mode("unsigned")) comparator_1 (
    .a(entrada2[30:0]), .b(entrada1[30:0]), .eq(comparator_1_eq), .lt(comparator_1_lt));  // open: gt
  Multiplexer multiplexer_1 (
    .in0(entrada2[31]), .in1(entrada1[31]), .out(EXPOENTE_MAIOR_NUMERO), .sel(comparator_1_lt), .en(En));
  Comparator #(.width(32)) comparator_2 (.a(entrada2), .b({32{1'b0}}), .eq(comparator_2_eq));  // open: gt, lt
  Comparator #(.width(32)) comparator_3 (.a(entrada2), .b(32'h80000000), .eq(comparator_3_eq));  // open: gt, lt
  Comparator #(.width(32)) comparator_4 (.a(entrada1), .b({32{1'b0}}), .eq(comparator_4_eq));  // open: gt, lt
  Comparator #(.width(32)) comparator_5 (.a(entrada1), .b(32'h80000000), .eq(comparator_5_eq));  // open: gt, lt
  or or_1 (or_1_out[0], comparator_2_eq, comparator_3_eq);
  or or_2 (or_1_out[1], comparator_4_eq, comparator_5_eq);
  Comparator #(.width(1), .mode("unsigned")) comparator_6 (
    .a(entrada2[31]), .b(entrada1[31]), .eq(comparator_6_eq));  // open: gt, lt
  or or_3 (out_3, or_1_out[1], and_1_out, or_1_out[0]);
  not not_1 (not_1_out, comparator_6_eq);
  Multiplexer #(.select(2), .width(32)) multiplexer_2 (
    .in0({32{1'b0}}), .in1(entrada1), .in2(entrada2), .in3({32{1'b0}}), .out(out_4), .sel(or_1_out),
    .en(out_3));
  and and_1 (and_1_out, comparator_1_eq, not_1_out);

  // Notes on the sheet:
  //   JUNTA EXPOENTE E MANTISSA
  //   PEGA OS DOIS EXPOENTES
endmodule

module Soma_Geral (
  input  enable,
  input  [31:0] v1,
  input  [31:0] v2,
  output [31:0] out_4,
  output OVERFLOW
);

  wire and_1_out, and_2_out, CASO_2_3, comparator_1_lt, comparator_2_lt, comparator_3_lt, comparator_4_gt,
       existe_ghost, existe_ghost_t, EXP, not_1_out, not_2_out, not_3_out, not_4_out, not_5_out, or_2_out,
       over_bit, overflow_caso_1_4, s1, s2, SINAL_MAIOR_NUMERO, underflow_caso_2_3;
  wire [0:0] or_1_out;
  wire [4:0] bitfinder_1_index, multiplexer_8_out, subtractor_4_out;
  wire [7:0] adder_1_out, adder_5_out, EXP1, EXP2, MAIOR_EXP, MENOR_EXP, multiplexer_11_out,
       subtractor_1_out, subtractor_2_out, subtractor_5_out;
  wire [22:0] adder_2_out, adder_3_out, adder_4_out, M1, M2, MANTISSA_DO_MAIOR_NUMERO,
       MANTISSA_DO_MENOR_NUMERO, multiplexer_9_out, multiplexer_10_out, shifter_1_out, shifter_2_out,
       shifter_3_out, shifter_4_out, shifter_5_out, subtractor_3_out;

  xor xor_1 (CASO_2_3, s1, s2);
  Multiplexer #(.width(32)) multiplexer_1 (.in1(v1), .out({s1, EXP1, M1}), .sel(enable), .en(enable));  // open: in0
  Multiplexer #(.width(32)) multiplexer_2 (.in1(v2), .out({s2, EXP2, M2}), .sel(enable), .en(enable));  // open: in0
  // Probe on EXP1
  // Probe on EXP2
  // Probe on M1
  // Probe on M2
  // Probe on {EXP1, M1}
  // Probe on {EXP2, M2}
  Comparator #(.mode("unsigned")) comparator_1 (.a(EXP1), .b(EXP2), .eq(EXP), .lt(comparator_1_lt));  // open: gt
  Comparator #(.mode("unsigned")) comparator_2 (.a(EXP1), .b(EXP2), .lt(comparator_2_lt));  // open: gt, eq
  Comparator #(.width(31), .mode("unsigned")) comparator_3 (
    .a({EXP1, M1}), .b({EXP2, M2}), .lt(comparator_3_lt));  // open: gt, eq
  Multiplexer multiplexer_3 (.in0(s1), .in1(s2), .out(SINAL_MAIOR_NUMERO), .sel(comparator_3_lt), .en(enable));
  Multiplexer #(.width(23)) multiplexer_4 (
    .in0(M1), .in1(M2), .out(MANTISSA_DO_MAIOR_NUMERO), .sel(comparator_3_lt), .en(enable));
  not not_1 (not_1_out, comparator_3_lt);
  Multiplexer #(.width(23)) multiplexer_5 (
    .in0(M1), .in1(M2), .out(MANTISSA_DO_MENOR_NUMERO), .sel(not_1_out), .en(enable));
  Multiplexer #(.width(8)) multiplexer_6 (.in0(EXP1), .in1(EXP2), .out(MAIOR_EXP), .sel(comparator_1_lt), .en(enable));
  not not_2 (not_2_out, comparator_2_lt);
  Multiplexer #(.width(8)) multiplexer_7 (.in0(EXP1), .in1(EXP2), .out(MENOR_EXP), .sel(not_2_out), .en(enable));
  Subtractor subtractor_1 (.a(MAIOR_EXP), .b(MENOR_EXP), .out(subtractor_1_out));  // open: bin, bout
  Shifter #(.width(23), .shift("lr")) shifter_1 (
    .in(MANTISSA_DO_MENOR_NUMERO), .\dist (multiplexer_8_out), .out(shifter_1_out));
  // Probe on subtractor_1_out
  Adder adder_1 (.a(subtractor_1_out), .b(MENOR_EXP), .out(adder_1_out));  // open: cin, cout
  // Probe on {3'b000, multiplexer_8_out}
  // Probe on s1
  // Probe on s2
  // Probe on adder_1_out
  // Probe on shifter_1_out
  Subtractor subtractor_2 (.a(8'h17), .b({3'b000, multiplexer_8_out}), .out(subtractor_2_out));  // open: bin, bout
  Comparator #(.mode("unsigned")) comparator_4 (.a(subtractor_1_out), .b(8'h17), .gt(comparator_4_gt));  // open: eq, lt
  // Probe on subtractor_2_out
  // Probe on subtractor_1_out[4:0]
  Multiplexer #(.width(5)) multiplexer_8 (
    .in0(subtractor_1_out[4:0]), .in1(5'b11000), .out(multiplexer_8_out), .sel(comparator_4_gt), .en(enable));
  // Probe on multiplexer_8_out
  // Probe on subtractor_2_out[4:0]
  Shifter #(.width(23)) shifter_2 (.in(23'h1), .\dist (subtractor_2_out[4:0]), .out(shifter_2_out));
  // Probe on shifter_2_out
  Adder #(.width(23)) adder_2 (.a(shifter_1_out), .b(shifter_2_out), .out(adder_2_out));  // open: cin, cout
  // Probe on adder_2_out
  // Probe on MANTISSA_DO_MAIOR_NUMERO
  // Probe on MANTISSA_DO_MAIOR_NUMERO
  Adder #(.width(23)) adder_3 (
    .a(adder_2_out), .b(MANTISSA_DO_MAIOR_NUMERO), .out(adder_3_out), .cout(over_bit));  // open: cin
  // Probe on {1'b1, MANTISSA_DO_MAIOR_NUMERO}
  // Probe on {EXP, adder_2_out}
  or or_1 (or_1_out[0], EXP, over_bit);
  and and_1 (and_1_out, EXP, over_bit);
  Shifter #(.width(23)) shifter_3 (.in(23'h1), .\dist (5'b10110), .out(shifter_3_out));
  // Probe on adder_3_out
  // Probe on {4'b0000, or_1_out[0]}
  Multiplexer #(.width(23)) multiplexer_9 (
    .in0({23{1'b0}}), .in1(shifter_3_out), .out(multiplexer_9_out), .sel(and_1_out), .en(enable));
  Subtractor #(.width(24)) subtractor_3 (
    .a({1'b1, MANTISSA_DO_MAIOR_NUMERO}), .b({EXP, adder_2_out}), .out({existe_ghost_t, subtractor_3_out}));  // open: bin, bout
  // Probe on multiplexer_9_out
  // Probe on subtractor_3_out
  Shifter #(.width(23), .shift("lr")) shifter_4 (
    .in(adder_3_out), .\dist ({4'b0000, or_1_out[0]}), .out(shifter_4_out));
  // Probe on adder_3_out
  // Probe on subtractor_3_out
  // Probe on {{7{1'b0}}, or_1_out[0]}
  Adder #(.width(23)) adder_4 (.a(shifter_4_out), .b(multiplexer_9_out), .out(adder_4_out));  // open: cin, cout
  Adder adder_5 (
    .a({{7{1'b0}}, or_1_out[0]}), .b(MAIOR_EXP), .out(adder_5_out), .cout(overflow_caso_1_4));  // open: cin
  // Probe on adder_4_out
  // Probe on adder_5_out
  BitFinder #(.width(23), .\type ("high1")) bitfinder_1 (
    .in(subtractor_3_out), .index(bitfinder_1_index));  // open: found
  // Probe on bitfinder_1_index
  Subtractor #(.width(5)) subtractor_4 (
    .a(5'b10111), .b(bitfinder_1_index), .out(subtractor_4_out));  // open: bin, bout
  // Probe on subtractor_4_out
  Shifter #(.width(23)) shifter_5 (.in(subtractor_3_out), .\dist (subtractor_4_out), .out(shifter_5_out));
  // Probe on {3'b000, subtractor_4_out}
  // Probe on shifter_5_out
  not not_3 (not_3_out, existe_ghost);
  Multiplexer #(.width(23)) multiplexer_10 (
    .in0(subtractor_3_out), .in1(shifter_5_out), .out(multiplexer_10_out), .sel(not_3_out), .en(enable));
  Subtractor subtractor_5 (
    .a(MAIOR_EXP), .b({3'b000, subtractor_4_out}), .out(subtractor_5_out), .bout(underflow_caso_2_3));  // open: bin
  // Probe on multiplexer_10_out
  not not_4 (not_4_out, existe_ghost);
  Multiplexer #(.width(8)) multiplexer_11 (
    .in0(MAIOR_EXP), .in1(subtractor_5_out), .out(multiplexer_11_out), .sel(not_4_out), .en(enable));
  // Probe on {s1, adder_5_out, adder_4_out}
  // Probe on {SINAL_MAIOR_NUMERO, multiplexer_11_out, multiplexer_10_out}
  not not_5 (not_5_out, existe_ghost);
  and and_2 (and_2_out, underflow_caso_2_3, CASO_2_3, not_5_out);
  Multiplexer #(.width(32)) multiplexer_12 (
    .in0({s1, adder_5_out, adder_4_out}), .in1({SINAL_MAIOR_NUMERO, multiplexer_11_out, multiplexer_10_out}),
    .out(out_4), .sel(CASO_2_3), .en(enable));
  or or_2 (or_2_out, and_2_out, overflow_caso_1_4);
  and and_3 (OVERFLOW, or_2_out, enable);
  // NOT_Gate not_6 is placed but not wired

  // Other names for the same wires on the sheet: En = enable

  // Notes on the sheet:
  //   FLAG PARA CASO 2-3
  //   JUNTA EXPOENTE E MANTISSA
  //   IMPORTANTE!!!
  //   EM CIMA : 1 BIT RESPONSAVEL PELO SINAL(PRIMEIRO  / SEGUDO NUMERO)
  //   MEIO 8 BITS DO EXPOENTE
  //   EM BAIXO 23 BITS DA PARTE FRACIONÁRIA(MANTISSA)
  //   PEGA O MENOR EXPOENTE
  //   PEGA O MAIOR EXPOENTE
  //   IGUALA O MENOR EXPOENTE AO MAIOR
  //   ROTAÇÃO DA MANTISSA DO NUMERO DE MENOR EXPOENTE
  //   DIFERENÇA ENTRE OS EXPOENTES
  //   PARTE DO CIRCUITO QUE CORRIGE O PROBLEMA DO PRIMEIRO BIT TER QUE SER UM NO PRIMEIRO DESLOCAMENTO À DIREITA
  //   exp=
  //   MANTISSA DO NÚMERO DE MENOR EXPOENTE
  //   ESSA É A MANTISSA QUE SERÁ DESLOCADA PARA A DIREITA
  //   MANTISSA DO MENOR NUMERO APOS ROTACIONAR PARA DIREITA
  //   ROTAÇÃO PARA ESQUERDA PARA RESOLVER O PROBLEMA DO 1(GHOST)
  //   SE A DIFERENÇA DOS EXPOENTES FOI MAIOR QUE 23
  //   BIT FANTASMA
  //   E ONDE ELE DEVE ESTAR
  //   MANTISSA FINAL DO NUMERO COM MENOR EXPOENTE
  //   rotação caso 1/4 overflow
  //   GHOST caso 1/4 overflow
  //   CRIA O GHOST QUE VAI PARA MESTISSA
  //   mantissa final NÃO NORMALIZADA 1-4
  //   mantissa final NÃO NORMALIZADA 2-3
  //   MANTISSA FINAL VAI PARA A NORMALIZAÇÃO DO CASO 1-4
  //   ROTACIONANDO PARA DIREITA A MANTISSA FINAL PARA NORMALIZAR
  //   MANTISSA FINAL VAI PARA A NORMALIZAÇÃO DO CASO 2-3
  //   SOMA GHOST DA NORMALIZAÇÃO
  //   MATISSA FINAL APÓS NORMALIZAÇÃO CASO 1-4
  //   NORMALIZAÇÃO DA MANTISSA COM OVER BIT
  //   EXPOENTE APÓS NORMALIZAÇÃO
  //   RESULTADO FINAL FINAL AGORA VAI
endmodule

module \Sinal_de_Operação  (
  input  [31:0] N2,
  input  \BIT_DE_OPERAÇÃO ,
  output [31:0] out_3
);

  xor xor_1 (out_3[31], N2[31], \BIT_DE_OPERAÇÃO );

  assign out_3[30:0] = N2[30:0];
endmodule

module \Soma_Subtração  (
  input  \bit_de_operação ,
  input  [31:0] entrada1,
  input  [31:0] entrada2,
  output [31:0] RESULTADO_FINAL,
  output OVERFLOW
);

  wire not_1_out, not_2_out, verifica_nulo_1_out_3;
  wire [31:0] \sinal_de_operação_1_out_3 , soma_geral_1_out_4, verifica_nulo_1_out_4;

  \Sinal_de_Operação  \sinal_de_operação_1  (
    .N2(entrada2), .\BIT_DE_OPERAÇÃO (\bit_de_operação ), .out_3(\sinal_de_operação_1_out_3 ));
  // Probe on \sinal_de_operação_1_out_3 
  Verifica_Nulo verifica_nulo_1 (
    .entrada2(entrada1), .entrada1(\sinal_de_operação_1_out_3 ), .out_4(verifica_nulo_1_out_4),
    .out_3(verifica_nulo_1_out_3));
  not not_1 (not_1_out, verifica_nulo_1_out_3);
  Soma_Geral soma_geral_1 (
    .v1(entrada1), .v2(\sinal_de_operação_1_out_3 ), .enable(not_1_out), .out_4(soma_geral_1_out_4),
    .OVERFLOW(OVERFLOW));
  // Probe on verifica_nulo_1_out_4
  not not_2 (not_2_out, verifica_nulo_1_out_3);
  Multiplexer #(.width(32)) multiplexer_1 (
    .in0(verifica_nulo_1_out_4), .in1(soma_geral_1_out_4), .out(RESULTADO_FINAL), .sel(not_2_out), .en(1'b1));
endmodule
